// Logisim project 3_bit_async_counter.circ as structural Verilog: 1 circuit, main circuit main
module main (
  input  in_1
);

  wire clock_1_out, j_k_ff_1_q, j_k_ff_1_qn, j_k_ff_2_q, j_k_ff_2_qn, j_k_ff_3_q, j_k_ff_3_qn, j_k_ff_4_q;

  Clock clock_1 (.out(clock_1_out));
  J_K_Flip_Flop j_k_ff_1 (
    .J(in_1), .K(in_1), .clk(clock_1_out), .Q(j_k_ff_1_q), .Qn(j_k_ff_1_qn));  // open: preset, reset
  J_K_Flip_Flop j_k_ff_2 (
    .J(in_1), .K(in_1), .clk(j_k_ff_1_qn), .Q(j_k_ff_2_q), .Qn(j_k_ff_2_qn));  // open: preset, reset
  LED led_1 (.in(j_k_ff_4_q));
  LED led_2 (.in(j_k_ff_3_q));
  LED led_3 (.in(j_k_ff_2_q));
  J_K_Flip_Flop j_k_ff_3 (
    .J(in_1), .K(in_1), .clk(j_k_ff_2_qn), .Q(j_k_ff_3_q), .Qn(j_k_ff_3_qn));  // open: preset, reset
  LED led_4 (.in(j_k_ff_1_q));
  J_K_Flip_Flop j_k_ff_4 (.J(in_1), .K(in_1), .clk(j_k_ff_3_qn), .Q(j_k_ff_4_q));  // open: Qn, preset, reset
endmodule
