// Logisim project half_adder_MOD15_counter_lab_final.circ as structural Verilog: 1 circuit, main circuit main
module main (
  input  in_1,
  input  in_2,
  input  in_3
);

  wire and_1_out, and_2_out, clock_1_out, j_k_ff_1_q, j_k_ff_1_qn, j_k_ff_2_q, j_k_ff_2_qn, j_k_ff_3_q,
       j_k_ff_3_qn, j_k_ff_4_q, or_1_out;

  Clock clock_1 (.out(clock_1_out));
  J_K_Flip_Flop j_k_ff_1 (
    .J(in_3), .K(in_3), .clk(clock_1_out), .Q(j_k_ff_1_q), .Qn(j_k_ff_1_qn), .reset(and_2_out));  // open: preset
  and and_1 (and_1_out, in_1, in_2);
  or or_1 (or_1_out, in_1, in_2);
  and and_2 (and_2_out, j_k_ff_1_q, j_k_ff_2_q, j_k_ff_3_q, j_k_ff_4_q);
  LED led_1 (.in(and_1_out));
  LED led_2 (.in(or_1_out));
  J_K_Flip_Flop j_k_ff_2 (
    .J(in_3), .K(in_3), .clk(j_k_ff_1_qn), .Q(j_k_ff_2_q), .Qn(j_k_ff_2_qn), .reset(and_2_out));  // open: preset
  J_K_Flip_Flop j_k_ff_3 (
    .J(in_3), .K(in_3), .clk(j_k_ff_2_qn), .Q(j_k_ff_3_q), .Qn(j_k_ff_3_qn), .reset(and_2_out));  // open: preset
  LED led_3 (.in(j_k_ff_4_q));
  J_K_Flip_Flop j_k_ff_4 (
    .J(in_3), .K(in_3), .clk(j_k_ff_3_qn), .Q(j_k_ff_4_q), .reset(and_2_out));  // open: Qn, preset
  LED led_4 (.in(j_k_ff_3_q));
  LED led_5 (.in(j_k_ff_2_q));
  LED led_6 (.in(j_k_ff_1_q));

  // Notes on the sheet:
  //   Carry Out
  //   Sum Out
endmodule
