// Logisim project ALU_Library.circ as structural Verilog
module L_4_bit_OR_Gate_c36e44c5 (
  input  [3:0] A,
  input  [3:0] B,
  output [3:0] O
);

  or or_1 (O[3], A[3], B[3]);
  or or_2 (O[2], A[2], B[2]);
  or or_3 (O[1], A[1], B[1]);
  or or_4 (O[0], A[0], B[0]);
endmodule

module L_4_bit_XOR_Gate_a7a1a714 (
  input  [3:0] A,
  input  [3:0] B,
  output [3:0] O
);

  xor xor_1 (O[3], A[3], B[3]);
  xor xor_2 (O[2], A[2], B[2]);
  xor xor_3 (O[1], A[1], B[1]);
  xor xor_4 (O[0], A[0], B[0]);
endmodule

module L_4_bit_Adder_Subtractor_b4215ae2 (
  input  [3:0] A,
  input  Sel,
  input  [3:0] B,
  output [3:0] O,
  output Carry
);

  wire fa_2_cout, fa_3_cout, fa_4_cout, xor_1_out, xor_2_out, xor_3_out, xor_4_out;

  xor xor_1 (xor_1_out, B[3], Sel);
  FA fa_1 (.b(A[3]), .Cin(fa_2_cout), .a(xor_1_out), .S(O[3]), .Cout(Carry));
  xor xor_2 (xor_2_out, B[2], Sel);
  FA fa_2 (.b(A[2]), .Cin(fa_3_cout), .a(xor_2_out), .S(O[2]), .Cout(fa_2_cout));
  xor xor_3 (xor_3_out, B[1], Sel);
  FA fa_3 (.b(A[1]), .Cin(fa_4_cout), .a(xor_3_out), .S(O[1]), .Cout(fa_3_cout));
  xor xor_4 (xor_4_out, B[0], Sel);
  FA fa_4 (.b(A[0]), .Cin(Sel), .a(xor_4_out), .S(O[0]), .Cout(fa_4_cout));
endmodule

module FA (
  input  a,
  input  b,
  input  Cin,
  output S,
  output Cout
);

  wire and_1_out, and_2_out, xor_1_out;

  xor xor_1 (xor_1_out, a, b);
  xor xor_2 (S, xor_1_out, Cin);
  and and_1 (and_1_out, Cin, xor_1_out);
  and and_2 (and_2_out, a, b);
  or or_1 (Cout, and_1_out, and_2_out);
endmodule

module L_4_bit_Left_Shifter_e418044b (
  input  [3:0] A,
  input  [1:0] Shift,
  output [3:0] O
);

  Multiplexer #(.select(2)) multiplexer_1 (.in0(A[3]), .in1(A[2]), .in2(A[1]), .in3(A[0]), .out(O[3]), .sel(Shift));
  Multiplexer #(.select(2)) multiplexer_2 (.in0(A[2]), .in1(A[1]), .in2(A[0]), .in3(1'b0), .out(O[2]), .sel(Shift));
  Multiplexer #(.select(2)) multiplexer_3 (.in0(A[1]), .in1(A[0]), .in2(1'b0), .in3(1'b0), .out(O[1]), .sel(Shift));
  Multiplexer #(.select(2)) multiplexer_4 (.in0(A[0]), .in1(1'b0), .in2(1'b0), .in3(1'b0), .out(O[0]), .sel(Shift));
endmodule

module L_4_bit_Right_Shifter_6f425c26 (
  input  [3:0] A,
  input  [1:0] Shift,
  output [3:0] O
);

  Multiplexer #(.select(2)) multiplexer_1 (.in0(A[3]), .in1(1'b0), .in2(1'b0), .in3(1'b0), .out(O[3]), .sel(Shift));
  Multiplexer #(.select(2)) multiplexer_2 (.in0(A[2]), .in1(A[3]), .in2(1'b0), .in3(1'b0), .out(O[2]), .sel(Shift));
  Multiplexer #(.select(2)) multiplexer_3 (.in0(A[1]), .in1(A[2]), .in2(A[3]), .in3(1'b0), .out(O[1]), .sel(Shift));
  Multiplexer #(.select(2)) multiplexer_4 (.in0(A[0]), .in1(A[1]), .in2(A[2]), .in3(A[3]), .out(O[0]), .sel(Shift));
endmodule

module L_4_Bit_Left_Rotate_c297eb02 (
  input  [3:0] A,
  input  [1:0] Shift,
  output [3:0] O
);

  Multiplexer #(.select(2)) multiplexer_1 (.in0(A[3]), .in1(A[2]), .in2(A[1]), .in3(A[0]), .out(O[3]), .sel(Shift));
  Multiplexer #(.select(2)) multiplexer_2 (.in0(A[2]), .in1(A[1]), .in2(A[0]), .in3(A[3]), .out(O[2]), .sel(Shift));
  Multiplexer #(.select(2)) multiplexer_3 (.in0(A[1]), .in1(A[0]), .in2(A[3]), .in3(A[2]), .out(O[1]), .sel(Shift));
  Multiplexer #(.select(2)) multiplexer_4 (.in0(A[0]), .in1(A[3]), .in2(A[2]), .in3(A[1]), .out(O[0]), .sel(Shift));
endmodule

module L_4_bit_Right_Rotate_956da996 (
  input  [3:0] A,
  input  [1:0] Shift,
  output [3:0] O
);

  Multiplexer #(.select(2)) multiplexer_1 (.in0(A[3]), .in1(A[0]), .in2(A[1]), .in3(A[2]), .out(O[3]), .sel(Shift));
  Multiplexer #(.select(2)) multiplexer_2 (.in0(A[2]), .in1(A[3]), .in2(A[0]), .in3(A[1]), .out(O[2]), .sel(Shift));
  Multiplexer #(.select(2)) multiplexer_3 (.in0(A[1]), .in1(A[2]), .in2(A[3]), .in3(A[0]), .out(O[1]), .sel(Shift));
  Multiplexer #(.select(2)) multiplexer_4 (.in0(A[0]), .in1(A[1]), .in2(A[2]), .in3(A[3]), .out(O[0]), .sel(Shift));
endmodule

module L_4_bit_NOT_Gate_8250c7bd (
  input  [3:0] in_1,
  output [3:0] out_2
);

  not not_1 (out_2[3], in_1[3]);
  not not_2 (out_2[2], in_1[2]);
  not not_3 (out_2[1], in_1[1]);
  not not_4 (out_2[0], in_1[0]);

  // Other names for the same wires on the sheet: A0 = in_1[0]; A1 = in_1[1]; A2 = in_1[2]; A3 = in_1[3];
  //   O0 = out_2[0]; O1 = out_2[1]; O2 = out_2[2]; O3 = out_2[3]
endmodule

module Cell_M (
  input  x,
  input  y,
  input  a,
  input  b,
  output Cout,
  output x_copy,
  output s
);

  wire and_1_out;

  and and_1 (and_1_out, x, y);
  FA fa_1 (.b(a), .Cin(b), .a(and_1_out), .S(s), .Cout(Cout));

  assign x_copy = x;
endmodule

module L_4_bit_Unsigned_Multiplier_7303e668 (
  input  [3:0] B,
  input  [3:0] A,
  output Overflow,
  output [3:0] O
);

  wire cell_m_1_cout, cell_m_1_s, cell_m_2_cout, cell_m_2_s, cell_m_2_x_copy, cell_m_3_cout, cell_m_3_s,
       cell_m_4_cout, cell_m_4_s, cell_m_4_x_copy, cell_m_5_cout, cell_m_5_s, cell_m_5_x_copy, cell_m_6_cout,
       cell_m_6_s, cell_m_7_cout, cell_m_7_s, cell_m_7_x_copy, cell_m_8_cout, cell_m_8_s, cell_m_8_x_copy,
       cell_m_9_cout, cell_m_9_s, cell_m_9_x_copy, cell_m_10_cout, cell_m_11_cout, cell_m_11_s,
       cell_m_11_x_copy, cell_m_12_cout, cell_m_12_s, cell_m_12_x_copy, cell_m_13_cout, cell_m_13_x_copy,
       cell_m_14_cout, cell_m_14_s, cell_m_14_x_copy, cell_m_15_cout, cell_m_15_x_copy, cell_m_16_cout,
       cell_m_16_x_copy;

  Cell_M cell_m_1 (
    .x(cell_m_2_x_copy), .y(B[3]), .a(cell_m_2_cout), .b(cell_m_3_cout), .Cout(cell_m_1_cout), .s(cell_m_1_s));  // open: x_copy
  or or_1 (Overflow, cell_m_1_cout, cell_m_1_s, cell_m_3_s, cell_m_6_s);
  Cell_M cell_m_2 (
    .x(cell_m_4_x_copy), .y(B[2]), .a(cell_m_4_cout), .b(cell_m_5_cout), .Cout(cell_m_2_cout),
    .x_copy(cell_m_2_x_copy), .s(cell_m_2_s));
  Cell_M cell_m_3 (
    .x(cell_m_5_x_copy), .y(B[3]), .a(cell_m_2_s), .b(cell_m_6_cout), .Cout(cell_m_3_cout), .s(cell_m_3_s));  // open: x_copy
  Cell_M cell_m_4 (
    .x(cell_m_7_x_copy), .y(B[1]), .a(cell_m_7_cout), .b(cell_m_8_cout), .Cout(cell_m_4_cout),
    .x_copy(cell_m_4_x_copy), .s(cell_m_4_s));
  Cell_M cell_m_5 (
    .x(cell_m_8_x_copy), .y(B[2]), .a(cell_m_4_s), .b(cell_m_9_cout), .Cout(cell_m_5_cout),
    .x_copy(cell_m_5_x_copy), .s(cell_m_5_s));
  Cell_M cell_m_6 (
    .x(cell_m_9_x_copy), .y(B[3]), .a(cell_m_5_s), .b(cell_m_10_cout), .Cout(cell_m_6_cout), .s(cell_m_6_s));  // open: x_copy
  Cell_M cell_m_7 (
    .x(A[3]), .y(B[0]), .a(1'b0), .b(cell_m_11_cout), .Cout(cell_m_7_cout), .x_copy(cell_m_7_x_copy),
    .s(cell_m_7_s));
  Cell_M cell_m_8 (
    .x(cell_m_11_x_copy), .y(B[1]), .a(cell_m_7_s), .b(cell_m_12_cout), .Cout(cell_m_8_cout),
    .x_copy(cell_m_8_x_copy), .s(cell_m_8_s));
  Cell_M cell_m_9 (
    .x(cell_m_12_x_copy), .y(B[2]), .a(cell_m_8_s), .b(cell_m_13_cout), .Cout(cell_m_9_cout),
    .x_copy(cell_m_9_x_copy), .s(cell_m_9_s));
  Cell_M cell_m_10 (
    .x(cell_m_13_x_copy), .y(B[3]), .a(cell_m_9_s), .b(1'b0), .Cout(cell_m_10_cout), .s(O[3]));  // open: x_copy
  Cell_M cell_m_11 (
    .x(A[2]), .y(B[0]), .a(1'b0), .b(cell_m_14_cout), .Cout(cell_m_11_cout), .x_copy(cell_m_11_x_copy),
    .s(cell_m_11_s));
  Cell_M cell_m_12 (
    .x(cell_m_14_x_copy), .y(B[1]), .a(cell_m_11_s), .b(cell_m_15_cout), .Cout(cell_m_12_cout),
    .x_copy(cell_m_12_x_copy), .s(cell_m_12_s));
  Cell_M cell_m_13 (
    .x(cell_m_15_x_copy), .y(B[2]), .a(cell_m_12_s), .b(1'b0), .Cout(cell_m_13_cout),
    .x_copy(cell_m_13_x_copy), .s(O[2]));
  Cell_M cell_m_14 (
    .x(A[1]), .y(B[0]), .a(1'b0), .b(cell_m_16_cout), .Cout(cell_m_14_cout), .x_copy(cell_m_14_x_copy),
    .s(cell_m_14_s));
  Cell_M cell_m_15 (
    .x(cell_m_16_x_copy), .y(B[1]), .a(cell_m_14_s), .b(1'b0), .Cout(cell_m_15_cout),
    .x_copy(cell_m_15_x_copy), .s(O[1]));
  Cell_M cell_m_16 (.x(A[0]), .y(B[0]), .a(1'b0), .b(1'b0), .Cout(cell_m_16_cout), .x_copy(cell_m_16_x_copy), .s(O[0]));
endmodule

module FS (
  input  A,
  input  B,
  input  Bin,
  output D,
  output Bout
);

  wire and_1_out, and_2_out, and_3_out, not_1_out, not_2_out, or_1_out, xor_1_out;

  xor xor_1 (xor_1_out, A, B);
  not not_1 (not_1_out, A);
  and and_1 (and_1_out, not_1_out, Bin);
  not not_2 (not_2_out, A);
  and and_2 (and_2_out, not_2_out, B);
  xor xor_2 (D, xor_1_out, Bin);
  or or_1 (or_1_out, and_1_out, and_2_out);
  and and_3 (and_3_out, B, Bin);
  or or_2 (Bout, or_1_out, and_3_out);
endmodule

module Cell_D (
  input  A,
  input  B,
  input  Bin,
  input  Sel,
  output Bout,
  output Sel_copy,
  output A_D_af025bf7,
  output B_copy
);

  wire fs_1_d;

  FS fs_1 (.A(A), .B(B), .Bin(Bin), .D(fs_1_d), .Bout(Bout));
  Multiplexer multiplexer_1 (.in0(fs_1_d), .in1(A), .out(A_D_af025bf7), .sel(Sel));

  assign B_copy = B;
  assign Sel_copy = Sel;
endmodule

module L_4_bit_Unsigned_Divider_c35b2005 (
  input  [3:0] A,
  input  [3:0] B,
  output Exception,
  output [3:0] O
);

  wire cell_d_1_b_copy, cell_d_1_bout, cell_d_1_sel_copy, cell_d_2_a_d_af025bf7, cell_d_2_b_copy,
       cell_d_2_bout, cell_d_2_sel_copy, cell_d_3_b_copy, cell_d_3_bout, cell_d_3_sel_copy,
       cell_d_4_a_d_af025bf7, cell_d_4_b_copy, cell_d_4_bout, cell_d_4_sel_copy, cell_d_5_a_d_af025bf7,
       cell_d_5_b_copy, cell_d_5_bout, cell_d_5_sel_copy, cell_d_6_b_copy, cell_d_6_bout, cell_d_6_sel_copy,
       cell_d_7_a_d_af025bf7, cell_d_7_b_copy, cell_d_7_bout, cell_d_8_a_d_af025bf7, cell_d_8_b_copy,
       cell_d_8_bout, cell_d_8_sel_copy, cell_d_9_a_d_af025bf7, cell_d_9_b_copy, cell_d_9_bout,
       cell_d_9_sel_copy, cell_d_10_bout, cell_d_10_sel_copy, cell_d_11_a_d_af025bf7, cell_d_11_b_copy,
       cell_d_11_bout, cell_d_12_a_d_af025bf7, cell_d_12_b_copy, cell_d_12_bout, cell_d_12_sel_copy,
       cell_d_13_bout, cell_d_13_sel_copy, cell_d_14_a_d_af025bf7, cell_d_14_b_copy, cell_d_14_bout,
       cell_d_15_bout, cell_d_15_sel_copy, cell_d_16_bout;

  not not_1 (O[3], cell_d_1_bout);
  Cell_D cell_d_1 (
    .Sel(cell_d_1_bout), .A(1'b0), .B(B[3]), .Bin(cell_d_2_bout), .Bout(cell_d_1_bout),
    .Sel_copy(cell_d_1_sel_copy), .B_copy(cell_d_1_b_copy));  // open: A_D_af025bf7
  not not_2 (O[2], cell_d_3_bout);
  Cell_D cell_d_2 (
    .Sel(cell_d_1_sel_copy), .A(1'b0), .B(B[2]), .Bin(cell_d_4_bout), .Bout(cell_d_2_bout),
    .A_D_af025bf7(cell_d_2_a_d_af025bf7), .Sel_copy(cell_d_2_sel_copy), .B_copy(cell_d_2_b_copy));
  Cell_D cell_d_3 (
    .Sel(cell_d_3_bout), .A(cell_d_2_a_d_af025bf7), .B(cell_d_1_b_copy), .Bin(cell_d_5_bout),
    .Bout(cell_d_3_bout), .Sel_copy(cell_d_3_sel_copy), .B_copy(cell_d_3_b_copy));  // open: A_D_af025bf7
  not not_3 (O[1], cell_d_6_bout);
  Cell_D cell_d_4 (
    .Sel(cell_d_2_sel_copy), .A(1'b0), .B(B[1]), .Bin(cell_d_7_bout), .Bout(cell_d_4_bout),
    .A_D_af025bf7(cell_d_4_a_d_af025bf7), .Sel_copy(cell_d_4_sel_copy), .B_copy(cell_d_4_b_copy));
  Cell_D cell_d_5 (
    .Sel(cell_d_3_sel_copy), .A(cell_d_4_a_d_af025bf7), .B(cell_d_2_b_copy), .Bin(cell_d_8_bout),
    .Bout(cell_d_5_bout), .A_D_af025bf7(cell_d_5_a_d_af025bf7), .Sel_copy(cell_d_5_sel_copy),
    .B_copy(cell_d_5_b_copy));
  Cell_D cell_d_6 (
    .Sel(cell_d_6_bout), .A(cell_d_5_a_d_af025bf7), .B(cell_d_3_b_copy), .Bin(cell_d_9_bout),
    .Bout(cell_d_6_bout), .Sel_copy(cell_d_6_sel_copy), .B_copy(cell_d_6_b_copy));  // open: A_D_af025bf7
  not not_4 (O[0], cell_d_10_bout);
  Cell_D cell_d_7 (
    .Sel(cell_d_4_sel_copy), .A(A[3]), .B(B[0]), .Bin(1'b0), .Bout(cell_d_7_bout),
    .A_D_af025bf7(cell_d_7_a_d_af025bf7), .B_copy(cell_d_7_b_copy));  // open: Sel_copy
  Cell_D cell_d_8 (
    .Sel(cell_d_5_sel_copy), .A(cell_d_7_a_d_af025bf7), .B(cell_d_4_b_copy), .Bin(cell_d_11_bout),
    .Bout(cell_d_8_bout), .A_D_af025bf7(cell_d_8_a_d_af025bf7), .Sel_copy(cell_d_8_sel_copy),
    .B_copy(cell_d_8_b_copy));
  Cell_D cell_d_9 (
    .Sel(cell_d_6_sel_copy), .A(cell_d_8_a_d_af025bf7), .B(cell_d_5_b_copy), .Bin(cell_d_12_bout),
    .Bout(cell_d_9_bout), .A_D_af025bf7(cell_d_9_a_d_af025bf7), .Sel_copy(cell_d_9_sel_copy),
    .B_copy(cell_d_9_b_copy));
  Cell_D cell_d_10 (
    .Sel(cell_d_10_bout), .A(cell_d_9_a_d_af025bf7), .B(cell_d_6_b_copy), .Bin(cell_d_13_bout),
    .Bout(cell_d_10_bout), .Sel_copy(cell_d_10_sel_copy));  // open: A_D_af025bf7, B_copy
  Cell_D cell_d_11 (
    .Sel(cell_d_8_sel_copy), .A(A[2]), .B(cell_d_7_b_copy), .Bin(1'b0), .Bout(cell_d_11_bout),
    .A_D_af025bf7(cell_d_11_a_d_af025bf7), .B_copy(cell_d_11_b_copy));  // open: Sel_copy
  Cell_D cell_d_12 (
    .Sel(cell_d_9_sel_copy), .A(cell_d_11_a_d_af025bf7), .B(cell_d_8_b_copy), .Bin(cell_d_14_bout),
    .Bout(cell_d_12_bout), .A_D_af025bf7(cell_d_12_a_d_af025bf7), .Sel_copy(cell_d_12_sel_copy),
    .B_copy(cell_d_12_b_copy));
  Cell_D cell_d_13 (
    .Sel(cell_d_10_sel_copy), .A(cell_d_12_a_d_af025bf7), .B(cell_d_9_b_copy), .Bin(cell_d_15_bout),
    .Bout(cell_d_13_bout), .Sel_copy(cell_d_13_sel_copy));  // open: A_D_af025bf7, B_copy
  Cell_D cell_d_14 (
    .Sel(cell_d_12_sel_copy), .A(A[1]), .B(cell_d_11_b_copy), .Bin(1'b0), .Bout(cell_d_14_bout),
    .A_D_af025bf7(cell_d_14_a_d_af025bf7), .B_copy(cell_d_14_b_copy));  // open: Sel_copy
  Cell_D cell_d_15 (
    .Sel(cell_d_13_sel_copy), .A(cell_d_14_a_d_af025bf7), .B(cell_d_12_b_copy), .Bin(cell_d_16_bout),
    .Bout(cell_d_15_bout), .Sel_copy(cell_d_15_sel_copy));  // open: A_D_af025bf7, B_copy
  nor nor_1 (Exception, B[3], B[2], B[1], B[0]);
  Cell_D cell_d_16 (
    .Sel(cell_d_15_sel_copy), .A(A[0]), .B(cell_d_14_b_copy), .Bin(1'b0), .Bout(cell_d_16_bout));  // open: A_D_af025bf7, Sel_copy, B_copy
endmodule

module ALU (
  input  [3:0] A_3_0_5dae2f2e,
  input  [3:0] B_3_0_84ffdd89,
  input  [3:0] OP_3_0_a8348dd2,
  output Carry_Flag_99e20942,
  output [3:0] R_3_0_84474f43,
  output Sign_Flag_4efeefec,
  output Zero_Flag_4495333b,
  output MUL_Excep_a8c6ef27,
  output DIV_Excep_b65a297f
);

  wire or_1_out;
  wire [3:0] ADD_SUB, AND, L_ROTATE, L_SHIFT, NOT, OR, R_ROTATE, R_SHIFT, U_DIV, U_MUL, XOR;

  L_4_bit_AND_Gate_433860f2 l_4_bit_and_gate_433860f2_1 ();
  L_4_bit_OR_Gate_c36e44c5 l_4_bit_or_gate_c36e44c5_1 (.A(A_3_0_5dae2f2e), .B(B_3_0_84ffdd89), .O(OR));
  L_4_bit_XOR_Gate_a7a1a714 l_4_bit_xor_gate_a7a1a714_1 (.A(A_3_0_5dae2f2e), .B(B_3_0_84ffdd89), .O(XOR));
  L_4_bit_Left_Shifter_e418044b l_4_bit_left_shifter_e418044b_1 (
    .Shift(B_3_0_84ffdd89[1:0]), .A(A_3_0_5dae2f2e), .O(L_SHIFT));
  L_4_bit_Right_Shifter_6f425c26 l_4_bit_right_shifter_6f425c26_1 (
    .Shift(B_3_0_84ffdd89[1:0]), .A(A_3_0_5dae2f2e), .O(R_SHIFT));
  L_4_bit_Adder_Subtractor_b4215ae2 l_4_bit_adder_subtractor_b4215ae2_1 (
    .Sel(OP_3_0_a8348dd2[1]), .A(A_3_0_5dae2f2e), .B(B_3_0_84ffdd89), .O(ADD_SUB), .Carry(Carry_Flag_99e20942));
  L_4_bit_Unsigned_Multiplier_7303e668 l_4_bit_unsigned_multiplier_7303e668_1 (
    .B(B_3_0_84ffdd89), .A(A_3_0_5dae2f2e), .Overflow(MUL_Excep_a8c6ef27), .O(U_MUL));
  L_4_Bit_Left_Rotate_c297eb02 l_4_bit_left_rotate_c297eb02_1 (
    .Shift(B_3_0_84ffdd89[1:0]), .A(A_3_0_5dae2f2e), .O(L_ROTATE));
  L_4_bit_Right_Rotate_956da996 l_4_bit_right_rotate_956da996_1 (
    .Shift(B_3_0_84ffdd89[1:0]), .A(A_3_0_5dae2f2e), .O(R_ROTATE));
  L_4_bit_NOT_Gate_8250c7bd l_4_bit_not_gate_8250c7bd_1 (.in_1(A_3_0_5dae2f2e), .out_2(NOT));
  L_4_bit_Unsigned_Divider_c35b2005 l_4_bit_unsigned_divider_c35b2005_1 (
    .B(B_3_0_84ffdd89), .A(A_3_0_5dae2f2e), .O(U_DIV), .Exception(DIV_Excep_b65a297f));
  Multiplexer #(.select(4), .width(4)) multiplexer_1 (
    .in0(AND), .in1(OR), .in2(XOR), .in3(L_SHIFT), .in4(R_SHIFT), .in5(ADD_SUB), .in6(ADD_SUB), .in7(U_MUL),
    .in8(L_ROTATE), .in9(R_ROTATE), .in10(NOT), .in11(ADD_SUB), .in12(U_DIV), .out(R_3_0_84474f43),
    .sel(OP_3_0_a8348dd2));  // open: in13, in14, in15
  or or_1 (or_1_out, R_3_0_84474f43[0], R_3_0_84474f43[1], R_3_0_84474f43[2], R_3_0_84474f43[3]);
  not not_1 (Zero_Flag_4495333b, or_1_out);

  assign Sign_Flag_4efeefec = R_3_0_84474f43[3];

  // Other names for the same wires on the sheet: A[3:0] = A_3_0_5dae2f2e; B[3:0] = B_3_0_84ffdd89;
  //   Shift[1:0] = B_3_0_84ffdd89[1:0]; ADD_SUB_Sel = OP_3_0_a8348dd2[1]
endmodule

module ALU_testing (
  input  [3:0] A,
  input  [3:0] B,
  input  [3:0] OP,
  output [3:0] R,
  output CF,
  output SF,
  output ZF,
  output DIV_Excep_b65a297f,
  output MUL_Excep_a8c6ef27
);

  ALU alu_1 (
    .A_3_0_5dae2f2e(A), .B_3_0_84ffdd89(B), .OP_3_0_a8348dd2(OP), .Carry_Flag_99e20942(CF),
    .R_3_0_84474f43(R), .Sign_Flag_4efeefec(SF), .Zero_Flag_4495333b(ZF),
    .MUL_Excep_a8c6ef27(MUL_Excep_a8c6ef27), .DIV_Excep_b65a297f(DIV_Excep_b65a297f));
endmodule
